# Fritzing sketch experiment1 (saved by Fritzing 0.9.2b)
breadboards: 1

parts:
  Part1 = Arduino Uno (Rev3)
  R1 = Resistor [tolerance=±5% resistance=1k package="2512 [SMD]"]
  R2 = PHOTOCELL [package=photocell]
  U1 = POT [package=3362u]
  DYP-ME003 = mystery part, 3 pins [chip_label=?]
  U3 = RELAY-2 [package=relay-g5v]
  DYP-ME4 = mystery part, 3 pins [chip_label=?]

nets:
  N1: Part1.A0, R1.Pin_0, R2.P$2
  N2: Part1.A1, U1.S
  N3: Part1.A4/SDA, DYP-ME4.pin2
  N4: Part1.D13/SCK, U3.2
  N5: Part1.GND, R1.Pin_1, U1.A, DYP-ME003.pin3, U3.1, DYP-ME4.pin3
  N6: Part1.D2, DYP-ME003.pin2
  N7: Part1.5V, R2.P$1, U1.E, DYP-ME003.pin1, DYP-ME4.pin1
